# Fritzing sketch temperature_schematic (saved by Fritzing 0.9.6b)
stripboards: 1

parts:
  IC1 = SHIFT REGISTER [package=dil16]
  Part1 = DHT22 module  # not connected
  U2 = ATTINY45 [package=dip]

nets:
  GND: IC1.GND, U2.GND
  VCC: IC1.SCL, IC1.VCC, U2.VCC
  N1: IC1.SCK, U2.PB2(SCK_ADC1)
  N2: IC1.RCK, U2.PB1(MISO)
  N3: IC1.G, U2.PB0(MOSI)
  N4: IC1.SER, U2.PB4(ADC2)
